// Logisim project PipelinedCore.circ as structural Verilog: 12 circuits, main circuit RVI 1cycle
module RVI_1cycle (
);

  wire alu_abstraction_1_alubranch, alu_branch_1_alubranch, ALUSrc, ALUSrcID, Branch, BranchID, clk,
       ex_mem_1_memtoreg_2, ex_mem_1_zero_2, EX_MEMRegWrite, id_ex_1_branch_2, id_ex_1_memtoreg_2,
       id_ex_1_memwrite_2, id_ex_1_regwrite_2, ID_EXMemRead, ID_EXWriteDir, IF_IDWrite, IFFlush,
       main_control_1_memwrite, main_control_1_regwrite, MemRead, MemReadID, MemtoReg, MemtoRegID, MemWrite,
       MemWriteID, or_1_out, PCSrc, PCWrite, RegWrite, RegWriteID, rst, Stall;
  wire [1:0] ForwardA, ForwardB;
  wire [4:0] ALUCtrl, ALUCtrlID, ex_mem_1_writedir_2, id_ex_1_readdir1_2, id_ex_1_readdir2_2,
       id_ex_1_writedir_2, mem_wb_1_writedir_2, ReadDir1, ReadDir2;
  wire [7:0] PC_q_2;
  wire [31:0] adder_1_out, adder_2_out, alu_abstraction_1_aluoutput, ex_mem_1_pcbranch_2, ex_mem_1_rs2_2,
       EX_MEMrd, id_ex_1_immediate_2, id_ex_1_instruction_2, id_ex_1_rs1_2, id_ex_1_rs2_2,
       if_id_1_instruction_2, if_id_1_pc_2, Imm, mem_wb_1_aluoutput_2, mem_wb_1_dataoutput_2, MEM_WBrd,
       multiplexer_1_out, multiplexer_4_out, multiplexer_5_out, PC_q, ram_1_data, register_file_1_readdata1,
       register_file_1_readdata2, rom_1_data;

  Clock Clock (.out(clk));
  Button Reset_Regs (.out(rst));
  Multiplexer #(.width(32), .enable("false")) multiplexer_1 (
    .in0(adder_1_out), .in1(adder_2_out), .out(multiplexer_1_out), .sel(PCSrc));
  Register #(.width(32)) PC (
    .D(multiplexer_1_out), .en(PCWrite), .Q({PC_q[31:10], PC_q_2, PC_q[1:0]}), .clk(clk), .clr(rst));
  Adder #(.width(32)) adder_1 (.a(32'h4), .b({PC_q[31:10], PC_q_2, PC_q[1:0]}), .out(adder_1_out));  // open: cin, cout
  ROM #(.dataWidth(32)) rom_1 (.addr(PC_q_2), .data(rom_1_data));  // open: sel
  IF_ID if_id_1 (
    .clk(clk), .rst(or_1_out), .Instruction(rom_1_data), .PC({PC_q[31:10], PC_q_2, PC_q[1:0]}),
    .Instruction_2({if_id_1_instruction_2[31:25], ReadDir2, ReadDir1, if_id_1_instruction_2[14:0]}),
    .PC_2(if_id_1_pc_2), .en(IF_IDWrite));
  or or_1 (or_1_out, IFFlush, rst);
  // Probe on {if_id_1_instruction_2[31:25], ReadDir2, ReadDir1, if_id_1_instruction_2[14:0]}
  Main_Control main_control_1 (
    .Instruction({if_id_1_instruction_2[31:25], ReadDir2, ReadDir1, if_id_1_instruction_2[14:0]}),
    .ALUSrc(ALUSrcID), .MemtoReg(MemtoRegID), .RegWrite(main_control_1_regwrite), .MemRead(MemReadID),
    .MemWrite(main_control_1_memwrite), .Branch(BranchID), .ALUCtrl(ALUCtrlID));
  ImmGen immgen_1 (
    .Instruction({if_id_1_instruction_2[31:25], ReadDir2, ReadDir1, if_id_1_instruction_2[14:0]}),
    .Immediate(Imm));
  Multiplexer #(.enable("false")) multiplexer_2 (
    .in0(main_control_1_regwrite), .in1(1'b0), .out(RegWriteID), .sel(Stall));
  Multiplexer #(.enable("false")) multiplexer_3 (
    .in0(main_control_1_memwrite), .in1(1'b0), .out(MemWriteID), .sel(Stall));
  // Probe on Imm
  Hazard_Detection hazard_detection_1 (
    .PCWrite(PCWrite), .ID_EXMemRead(ID_EXMemRead), .IFWrite(IF_IDWrite),
    .Instruction({if_id_1_instruction_2[31:25], ReadDir2, ReadDir1, if_id_1_instruction_2[14:0]}),
    .Stall(Stall), .Flush(IFFlush), .ID_EXWriteDir(ID_EXWriteDir));
  Register_File register_file_1 (
    .clk(clk), .rst(rst), .ReadData1(register_file_1_readdata1), .ReadData2(register_file_1_readdata2),
    .WriteEn(RegWrite), .WriteDir(mem_wb_1_writedir_2), .WriteData(MEM_WBrd), .ReadDir1(ReadDir1),
    .ReadDir2(ReadDir2));
  Adder #(.width(32)) adder_2 (.a(if_id_1_pc_2), .b(Imm), .out(adder_2_out));  // open: cin, cout
  and and_1 (PCSrc, alu_branch_1_alubranch, Branch);
  ALU_Branch alu_branch_1 (
    .ALUBranch(alu_branch_1_alubranch), .a(register_file_1_readdata1), .b(register_file_1_readdata2),
    .ALUCtrl(ALUCtrlID));
  ID_EX id_ex_1 (
    .clk(clk), .rst(rst), .rs1(register_file_1_readdata1), .rs1_2(id_ex_1_rs1_2),
    .rs2(register_file_1_readdata2), .rs2_2(id_ex_1_rs2_2), .Immediate(Imm),
    .Immediate_2(id_ex_1_immediate_2), .PC(if_id_1_pc_2),
    .Instruction({if_id_1_instruction_2[31:25], ReadDir2, ReadDir1, if_id_1_instruction_2[14:0]}),
    .Instruction_2(id_ex_1_instruction_2), .WriteDir(if_id_1_instruction_2[11:7]),
    .WriteDir_2(id_ex_1_writedir_2), .ALUSrc(ALUSrcID), .ALUSrc_2(ALUSrc), .ALUOp(ALUCtrlID),
    .ALUOp_2(ALUCtrl), .Branch(BranchID), .Branch_2(id_ex_1_branch_2), .MemWrite(MemWriteID),
    .MemWrite_2(id_ex_1_memwrite_2), .MemRead(MemReadID), .MemRead_2(ID_EXMemRead), .RegWrite(RegWriteID),
    .RegWrite_2(id_ex_1_regwrite_2), .MemtoReg(MemtoRegID), .MemtoReg_2(id_ex_1_memtoreg_2),
    .ReadDir1(ReadDir1), .ReadDir1_2(id_ex_1_readdir1_2), .ReadDir2(ReadDir2), .ReadDir2_2(id_ex_1_readdir2_2));  // open: PC_2
  // Probe on id_ex_1_rs2_2
  // Probe on multiplexer_4_out
  Multiplexer #(.select(2), .width(32), .enable("false")) multiplexer_4 (
    .in0(id_ex_1_rs1_2), .in1(EX_MEMrd), .in2(MEM_WBrd), .out(multiplexer_4_out), .sel(ForwardA));  // open: in3
  Multiplexer #(.select(2), .width(32), .enable("false")) multiplexer_5 (
    .in0(id_ex_1_rs2_2), .in1(EX_MEMrd), .in2(MEM_WBrd), .in3(id_ex_1_immediate_2), .out(multiplexer_5_out),
    .sel(ForwardB));
  // Probe on multiplexer_5_out
  Forwarding forwarding_1 (
    .ReadDir1(id_ex_1_readdir1_2), .EX_MEMrd(EX_MEMrd), .MEM_WBrd(MEM_WBrd), .ReadDir2(id_ex_1_readdir2_2),
    .EX_MEMRegWrite(EX_MEMRegWrite), .MEM_WBRegWrite(RegWrite), .ForwardA(ForwardA), .ForwardB(ForwardB),
    .ALUsrc(ALUSrc));
  ALU_Abstraction alu_abstraction_1 (
    .ALUOutput(alu_abstraction_1_aluoutput), .ALUBranch(alu_abstraction_1_alubranch), .a(multiplexer_4_out),
    .b(multiplexer_5_out), .ALUCtrl(ALUCtrl));
  EX_MEM ex_mem_1 (
    .clk(clk), .rst(rst), .PCBranch_2(ex_mem_1_pcbranch_2), .Zero(alu_abstraction_1_alubranch),
    .Zero_2(ex_mem_1_zero_2), .ALUOutput(alu_abstraction_1_aluoutput), .ALUOutput_2(EX_MEMrd),
    .rs2(id_ex_1_rs2_2), .rs2_2(ex_mem_1_rs2_2), .WriteDir(id_ex_1_writedir_2),
    .WriteDir_2(ex_mem_1_writedir_2), .RegWrite(id_ex_1_regwrite_2), .RegWrite_2(EX_MEMRegWrite),
    .MemtoReg(id_ex_1_memtoreg_2), .MemtoReg_2(ex_mem_1_memtoreg_2), .Branch(id_ex_1_branch_2),
    .Branch_2(Branch), .MemWrite(id_ex_1_memwrite_2), .MemWrite_2(MemWrite), .MemRead(ID_EXMemRead),
    .MemRead_2(MemRead));  // open: PCBranch
  RAM #(.dataWidth(32), .bus("separate")) ram_1 (
    .addr(EX_MEMrd[9:2]), .din(ex_mem_1_rs2_2), .data(ram_1_data), .str(MemWrite), .clk(clk), .ld(MemRead));  // open: sel, clr
  // Probe on EX_MEMrd
  // Probe on ram_1_data
  MEM_WB mem_wb_1 (
    .clk(clk), .rst(rst), .ALUOutput(EX_MEMrd), .ALUOutput_2(mem_wb_1_aluoutput_2), .DataOutput(ram_1_data),
    .DataOutput_2(mem_wb_1_dataoutput_2), .WriteDir(ex_mem_1_writedir_2), .WriteDir_2(mem_wb_1_writedir_2),
    .RegWrite(EX_MEMRegWrite), .RegWrite_2(RegWrite), .MemtoReg(ex_mem_1_memtoreg_2), .MemtoReg_2(MemtoReg));
  Multiplexer #(.width(32), .enable("false")) multiplexer_6 (
    .in0(mem_wb_1_aluoutput_2), .in1(mem_wb_1_dataoutput_2), .out(MEM_WBrd), .sel(MemtoReg));
  // Probe on MEM_WBrd

  // Notes on the sheet:
  //   PCNext
  //   PCPlus4
  //   PC
  //   Alineado a word (1:0 = 0)
  //   Instruction
  //   contents of rom_1 (hex, n*v repeats v):
  //   52503 45a583 a58633 c2a223 2b60063 40b606b3 40d60633 b60a63 4*0 c6f6b3 c6e733
  //   PC
  //   Instruction
  //   Immediate
  //   Instruction
  //   WriteDir
  //   Instruction
  //   Stall
  //   Flush
  //   PC
  //   rs1
  //   rs2
  //   ReadDir1
  //   ReadDir2
  //   PC
  //   Branch
  //   ALUBranch
  //   ALUOutput
  //   Branching moved to ID stage
  //   Reduce cost of missprediction
  //   Alineado a word (1:0 = 0)
  //   ALUOutput
  //   DataOutput
  //   rd
endmodule

module Main_Control (
  input  [31:0] Instruction,
  output ALUSrc,
  output MemtoReg,
  output RegWrite,
  output MemRead,
  output MemWrite,
  output Branch,
  output [4:0] ALUCtrl
);

  wire lw_out, or_1_out, or_2_out, sw_out;
  wire [1:0] beq_out;
  wire [6:0] undriven;

  and R (beq_out[1], ~undriven[6], undriven[5], undriven[4], ~undriven[3], ~undriven[2], undriven[1], undriven[0]);  // AND_Gate
  and lw (lw_out, ~undriven[6], ~undriven[5], ~undriven[4], ~undriven[3], ~undriven[2], undriven[1], undriven[0]);  // AND_Gate
  and sw (sw_out, ~undriven[6], undriven[5], ~undriven[4], ~undriven[3], ~undriven[2], undriven[1], undriven[0]);  // AND_Gate
  and beq (beq_out[0], undriven[6], undriven[5], ~undriven[4], ~undriven[3], ~undriven[2], undriven[1], undriven[0]);  // AND_Gate
  or or_1 (or_1_out, lw_out, sw_out);
  or or_2 (or_2_out, beq_out[1], lw_out);

  // Notes on the sheet:
  //   Opcode
  //   func3
  //   func7
endmodule

module Register_File (
  input  [4:0] ReadDir1,
  input  [4:0] ReadDir2,
  input  WriteEn,
  input  [4:0] WriteDir,
  input  [31:0] WriteData,
  input  clk,
  input  rst,
  output [31:0] ReadData1,
  output [31:0] ReadData2
);

  wire [15:0] decoder_1_out0, decoder_1_out16;
  wire [31:0] x1___ra_q, x2___sp_q, x3___gp_q, x4___tp_q, x5___t0_q, x6___t1_q, x7___t2_q, x8___s0___fp_q,
       x9___s1_q, x10___a0_q, x11___a1_q, x12___a2_q, x13___a3_q, x14___a4_q, x15___a5_q, x16___a6_q,
       x17___a7_q, x18___s2_q, x19___s3_q, x20___s4_q, x21___s5_q, x22___s6_q, x23___s7_q, x24___s8_q,
       x25___s9_q, x26___s10_q, x27___s11_q, x28___t3_q, x29___t4_q, x30___t5_q, x31___t6_q;

  Decoder #(.select(5), .disabled(0)) decoder_1 (
    .out0(decoder_1_out0[0]), .out1(decoder_1_out0[1]), .out2(decoder_1_out0[2]), .out3(decoder_1_out0[3]),
    .out4(decoder_1_out0[4]), .out5(decoder_1_out0[5]), .out6(decoder_1_out0[6]), .out7(decoder_1_out0[7]),
    .out8(decoder_1_out0[8]), .out9(decoder_1_out0[9]), .out10(decoder_1_out0[10]),
    .out11(decoder_1_out0[11]), .out12(decoder_1_out0[12]), .out13(decoder_1_out0[13]),
    .out14(decoder_1_out0[14]), .out15(decoder_1_out0[15]), .out16(decoder_1_out16[0]),
    .out17(decoder_1_out16[1]), .out18(decoder_1_out16[2]), .out19(decoder_1_out16[3]),
    .out20(decoder_1_out16[4]), .out21(decoder_1_out16[5]), .out22(decoder_1_out16[6]),
    .out23(decoder_1_out16[7]), .out24(decoder_1_out16[8]), .out25(decoder_1_out16[9]),
    .out26(decoder_1_out16[10]), .out27(decoder_1_out16[11]), .out28(decoder_1_out16[12]),
    .out29(decoder_1_out16[13]), .out30(decoder_1_out16[14]), .out31(decoder_1_out16[15]), .sel(WriteDir),
    .en(WriteEn));
  // Probe on decoder_1_out0
  // Probe on WriteDir
  Register #(.width(32)) x1___ra (.D(WriteData), .en(decoder_1_out0[1]), .Q(x1___ra_q), .clk(clk), .clr(rst));
  Register #(.width(32)) x2___sp (.D(WriteData), .en(decoder_1_out0[2]), .Q(x2___sp_q), .clk(clk), .clr(rst));
  Register #(.width(32)) x3___gp (.D(WriteData), .en(decoder_1_out0[3]), .Q(x3___gp_q), .clk(clk), .clr(rst));
  Register #(.width(32)) x4___tp (.D(WriteData), .en(decoder_1_out0[4]), .Q(x4___tp_q), .clk(clk), .clr(rst));
  Register #(.width(32)) x5___t0 (.D(WriteData), .en(decoder_1_out0[5]), .Q(x5___t0_q), .clk(clk), .clr(rst));
  Register #(.width(32)) x6___t1 (.D(WriteData), .en(decoder_1_out0[6]), .Q(x6___t1_q), .clk(clk), .clr(rst));
  Register #(.width(32)) x7___t2 (.D(WriteData), .en(decoder_1_out0[7]), .Q(x7___t2_q), .clk(clk), .clr(rst));
  Register #(.width(32)) x8___s0___fp (.D(WriteData), .en(decoder_1_out0[8]), .Q(x8___s0___fp_q), .clk(clk), .clr(rst));
  Register #(.width(32)) x9___s1 (.D(WriteData), .en(decoder_1_out0[9]), .Q(x9___s1_q), .clk(clk), .clr(rst));
  Register #(.width(32)) x10___a0 (.D(WriteData), .en(decoder_1_out0[10]), .Q(x10___a0_q), .clk(clk), .clr(rst));
  Register #(.width(32)) x11___a1 (.D(WriteData), .en(decoder_1_out0[11]), .Q(x11___a1_q), .clk(clk), .clr(rst));
  Register #(.width(32)) x12___a2 (.D(WriteData), .en(decoder_1_out0[12]), .Q(x12___a2_q), .clk(clk), .clr(rst));
  Register #(.width(32)) x13___a3 (.D(WriteData), .en(decoder_1_out0[13]), .Q(x13___a3_q), .clk(clk), .clr(rst));
  Register #(.width(32)) x14___a4 (.D(WriteData), .en(decoder_1_out0[14]), .Q(x14___a4_q), .clk(clk), .clr(rst));
  Register #(.width(32)) x15___a5 (.D(WriteData), .en(decoder_1_out0[15]), .Q(x15___a5_q), .clk(clk), .clr(rst));
  // Probe on x13___a3_q
  Register #(.width(32)) x16___a6 (.D(WriteData), .en(decoder_1_out16[0]), .Q(x16___a6_q), .clk(clk), .clr(rst));
  Register #(.width(32)) x17___a7 (.D(WriteData), .en(decoder_1_out16[1]), .Q(x17___a7_q), .clk(clk), .clr(rst));
  Register #(.width(32)) x18___s2 (.D(WriteData), .en(decoder_1_out16[2]), .Q(x18___s2_q), .clk(clk), .clr(rst));
  Register #(.width(32)) x19___s3 (.D(WriteData), .en(decoder_1_out16[3]), .Q(x19___s3_q), .clk(clk), .clr(rst));
  Register #(.width(32)) x20___s4 (.D(WriteData), .en(decoder_1_out16[4]), .Q(x20___s4_q), .clk(clk), .clr(rst));
  Register #(.width(32)) x21___s5 (.D(WriteData), .en(decoder_1_out16[5]), .Q(x21___s5_q), .clk(clk), .clr(rst));
  Register #(.width(32)) x22___s6 (.D(WriteData), .en(decoder_1_out16[6]), .Q(x22___s6_q), .clk(clk), .clr(rst));
  Register #(.width(32)) x23___s7 (.D(WriteData), .en(decoder_1_out16[7]), .Q(x23___s7_q), .clk(clk), .clr(rst));
  Register #(.width(32)) x24___s8 (.D(WriteData), .en(decoder_1_out16[8]), .Q(x24___s8_q), .clk(clk), .clr(rst));
  Register #(.width(32)) x25___s9 (.D(WriteData), .en(decoder_1_out16[9]), .Q(x25___s9_q), .clk(clk), .clr(rst));
  Register #(.width(32)) x26___s10 (.D(WriteData), .en(decoder_1_out16[10]), .Q(x26___s10_q), .clk(clk), .clr(rst));
  Register #(.width(32)) x27___s11 (.D(WriteData), .en(decoder_1_out16[11]), .Q(x27___s11_q), .clk(clk), .clr(rst));
  Register #(.width(32)) x28___t3 (.D(WriteData), .en(decoder_1_out16[12]), .Q(x28___t3_q), .clk(clk), .clr(rst));
  Register #(.width(32)) x29___t4 (.D(WriteData), .en(decoder_1_out16[13]), .Q(x29___t4_q), .clk(clk), .clr(rst));
  Register #(.width(32)) x30___t5 (.D(WriteData), .en(decoder_1_out16[14]), .Q(x30___t5_q), .clk(clk), .clr(rst));
  Register #(.width(32)) x31___t6 (.D(WriteData), .en(decoder_1_out16[15]), .Q(x31___t6_q), .clk(clk), .clr(rst));
  Multiplexer #(.select(5), .width(32), .enable("false")) multiplexer_1 (
    .in0({32{1'b0}}), .in1(x1___ra_q), .in2(x2___sp_q), .in3(x3___gp_q), .in4(x4___tp_q), .in5(x5___t0_q),
    .in6(x6___t1_q), .in7(x7___t2_q), .in8(x8___s0___fp_q), .in9(x9___s1_q), .in10(x10___a0_q),
    .in11(x11___a1_q), .in12(x12___a2_q), .in13(x13___a3_q), .in14(x14___a4_q), .in15(x15___a5_q),
    .in16(x16___a6_q), .in17(x17___a7_q), .in18(x18___s2_q), .in19(x19___s3_q), .in20(x20___s4_q),
    .in21(x21___s5_q), .in22(x22___s6_q), .in23(x23___s7_q), .in24(x24___s8_q), .in25(x25___s9_q),
    .in26(x26___s10_q), .in27(x27___s11_q), .in28(x28___t3_q), .in29(x29___t4_q), .in30(x30___t5_q),
    .in31(x31___t6_q), .out(ReadData1), .sel(ReadDir1));
  Multiplexer #(.select(5), .width(32), .enable("false")) multiplexer_2 (
    .in0({32{1'b0}}), .in1(x1___ra_q), .in2(x2___sp_q), .in3(x3___gp_q), .in4(x4___tp_q), .in5(x5___t0_q),
    .in6(x6___t1_q), .in7(x7___t2_q), .in8(x8___s0___fp_q), .in9(x9___s1_q), .in10(x10___a0_q),
    .in11(x11___a1_q), .in12(x12___a2_q), .in13(x13___a3_q), .in14(x14___a4_q), .in15(x15___a5_q),
    .in16(x16___a6_q), .in17(x17___a7_q), .in18(x18___s2_q), .in19(x19___s3_q), .in20(x20___s4_q),
    .in21(x21___s5_q), .in22(x22___s6_q), .in23(x23___s7_q), .in24(x24___s8_q), .in25(x25___s9_q),
    .in26(x26___s10_q), .in27(x27___s11_q), .in28(x28___t3_q), .in29(x29___t4_q), .in30(x30___t5_q),
    .in31(x31___t6_q), .out(ReadData2), .sel(ReadDir2));

  // Notes on the sheet:
  //   WriteReg
  //   If not not-floating,
  //   when disabled, it can lead to
  //   write all regs
  //   x0 - zero
endmodule

module ALU_Abstraction (
  input  [31:0] a,
  input  [31:0] b,
  input  [4:0] ALUCtrl,
  output [31:0] ALUOutput,
  output ALUBranch
);

  wire comparator_3_gt, comparator_4_eq, comparator_4_lt;
  wire [0:0] beq, bge, bgeu, blt, bltu, bne, slt, sltu;
  wire [31:0] add, \and , \or , sll, sra, srl, sub, \xor ;

  Adder #(.width(32)) adder_1 (.a(a), .b(b), .out(add));  // open: cin, cout
  Subtractor #(.width(32)) subtractor_1 (.a(a), .b(b), .out(sub));  // open: bin, bout
  Shifter #(.width(32)) shifter_1 (.in(a), .\dist (b[4:0]), .out(sll));
  Comparator #(.width(32)) comparator_1 (.a(a), .b(b), .lt(slt[0]));  // open: gt, eq
  Comparator #(.width(32)) comparator_2 (.a(a), .b(b), .lt(sltu[0]));  // open: gt, eq
  assign \xor  = a ^ b;  // XOR_Gate xor_1, 32 bits wide
  Shifter #(.width(32), .shift("lr")) shifter_2 (.in(a), .\dist (b[4:0]), .out(srl));
  Shifter #(.width(32), .shift("ar")) shifter_3 (.in(a), .\dist (b[4:0]), .out(sra));
  assign \or  = a | b;  // OR_Gate or_1, 32 bits wide
  assign \and  = a & b;  // AND_Gate and_1, 32 bits wide
  Comparator #(.width(32)) comparator_3 (.a(a), .b(b), .gt(comparator_3_gt), .eq(beq[0]), .lt(blt[0]));
  Comparator #(.width(32), .mode("unsigned")) comparator_4 (
    .a(a), .b(b), .gt(bltu[0]), .eq(comparator_4_eq), .lt(comparator_4_lt));
  not not_1 (bne[0], beq[0]);
  or or_2 (bge[0], comparator_3_gt, beq[0]);
  or or_3 (bgeu[0], bltu[0], comparator_4_eq);
  Multiplexer #(.select(5), .width(32), .enable("false")) multiplexer_1 (
    .out({ALUOutput[31:1], ALUBranch}), .sel(ALUCtrl));  // open: in0, in1, in2, in3, in4, in5, in6, in7, in8, in9, in10, in11, in12, in13, in14, in15, in16, in17, in18, in19, in20, in21, in22, in23, in24, in25, in26, in27, in28, in29, in30, in31

  assign ALUOutput[0] = ALUBranch;

  // Notes on the sheet:
  //   add, addi
  //   sub
  //   sll
  //   slt, slti
  //   sltu, sltiu
  //   xor, xori
  //   srl, srli
  //   sra, srai
  //   or, ori
  //   and, andi
  //   Signed
  //   Unsigned
  //   beq
  //   bne
  //   blt
  //   bge
  //   bltu
  //   bgeu
endmodule

module ALU_Branch (
  input  [31:0] a,
  input  [31:0] b,
  input  [4:0] ALUCtrl,
  output ALUBranch
);

  wire comparator_1_gt, comparator_2_eq, comparator_2_lt;
  wire [0:0] beq, bge, bgeu, blt, bltu, bne;
  wire [31:1] multiplexer_1_out;

  Comparator #(.width(32)) comparator_1 (.a(a), .b(b), .gt(comparator_1_gt), .eq(beq[0]), .lt(blt[0]));
  Comparator #(.width(32), .mode("unsigned")) comparator_2 (
    .a(a), .b(b), .gt(bltu[0]), .eq(comparator_2_eq), .lt(comparator_2_lt));
  not not_1 (bne[0], beq[0]);
  or or_1 (bge[0], comparator_1_gt, beq[0]);
  or or_2 (bgeu[0], bltu[0], comparator_2_eq);
  Multiplexer #(.select(5), .width(32), .enable("false")) multiplexer_1 (
    .out({multiplexer_1_out, ALUBranch}), .sel(ALUCtrl));  // open: in0, in1, in2, in3, in4, in5, in6, in7, in8, in9, in10, in11, in12, in13, in14, in15, in16, in17, in18, in19, in20, in21, in22, in23, in24, in25, in26, in27, in28, in29, in30, in31

  // Notes on the sheet:
  //   Signed
  //   Unsigned
  //   beq
  //   bne
  //   blt
  //   bge
  //   bltu
  //   bgeu
endmodule

module ImmGen (
  input  [31:0] Instruction,
  output [31:0] Immediate
);

  wire [31:0] bit_extender_1_out, Btype, Itype, Jtype, shifter_1_out, Stype;

  Bit_Extender #(.in_width(20), .out_width(32), .\type ("sign")) bit_extender_1 (.out(bit_extender_1_out));  // open: in
  Shifter #(.width(32)) shifter_1 (.in(bit_extender_1_out), .\dist (5'b01100), .out(shifter_1_out));
  assign Stype = {{20{Instruction[31]}}, {Instruction[31:25], Instruction[11:7]}};  // Bit_Extender bit_extender_2
  assign Btype = {{19{Instruction[31]}}, {Instruction[31], Instruction[7], Instruction[30:25], Instruction[11:8], 1'b0}};  // Bit_Extender bit_extender_3
  assign Jtype = {{11{Instruction[31]}}, {Instruction[31], Instruction[19:12], Instruction[20], Instruction[30:21], 1'b0}};  // Bit_Extender bit_extender_4
  assign Itype = {{20{Instruction[31]}}, Instruction[31:20]};  // Bit_Extender bit_extender_5
  // Probe on Stype
  // Probe on Btype
  // Probe on {Instruction[31:12], {12{1'b0}}}
  // Probe on Jtype
  // Probe on Itype
  Multiplexer #(.select(5), .width(32), .enable("false")) multiplexer_1 (
    .in0(Itype), .in3(Itype), .in4(Itype), .in5({Instruction[31:12], {12{1'b0}}}), .in8(Stype),
    .in13({Instruction[31:12], {12{1'b0}}}), .in24(Btype), .in25(Itype), .in27(Jtype), .in28(Itype),
    .out(Immediate), .sel(Instruction[6:2]));  // open: in1, in2, in6, in7, in9, in10, in11, in12, in14, in15, in16, in17, in18, in19, in20, in21, in22, in23, in26, in29, in30, in31
  // Probe on Instruction[6:2]

  // Other names for the same wires on the sheet: Utype[31:12] = Instruction[31:12]

  // Notes on the sheet:
  //   "Sign Extend" [19:0] = 0
  //   Calculate all posibilities of immediates and select one of them based on opcode
  //   Use control lines to implement what of the immediates is being to be generated
  //   From this 2 options the second one seems to increment the complexity of the desing while the first one don't implicitly reduces its performance
  //   Bits 2-6 of opcode
  //   Loads
  //   fence
  //   Arithmetics
  //   aupic
  //   Stores
  //   lui
  //   Branches
  //   jalr
  //   jal
  //   ecall/ebreak
endmodule

module IF_ID (
  input  clk,
  input  rst,
  input  en,
  input  [31:0] PC,
  input  [31:0] Instruction,
  output [31:0] PC_2,
  output [31:0] Instruction_2
);

  Register #(.width(32)) register_1 (.D(PC), .en(en), .Q(PC_2), .clk(clk), .clr(rst));
  Register #(.width(32)) register_2 (.D(Instruction), .en(en), .Q(Instruction_2), .clk(clk), .clr(rst));
endmodule

module ID_EX (
  input  clk,
  input  rst,
  input  [31:0] PC,
  input  RegWrite,
  input  MemtoReg,
  input  [31:0] rs1,
  input  Branch,
  input  [31:0] rs2,
  input  MemWrite,
  input  [31:0] Immediate,
  input  MemRead,
  input  [31:0] Instruction,
  input  ALUSrc,
  input  [4:0] WriteDir,
  input  [4:0] ALUOp,
  input  [4:0] ReadDir1,
  input  [4:0] ReadDir2,
  output [31:0] PC_2,
  output RegWrite_2,
  output MemtoReg_2,
  output [31:0] rs1_2,
  output Branch_2,
  output [31:0] rs2_2,
  output MemWrite_2,
  output [31:0] Immediate_2,
  output MemRead_2,
  output [31:0] Instruction_2,
  output ALUSrc_2,
  output [4:0] WriteDir_2,
  output [4:0] ALUOp_2,
  output [4:0] ReadDir1_2,
  output [4:0] ReadDir2_2
);

  Register #(.width(32)) register_1 (.D(PC), .Q(PC_2), .clk(clk), .clr(rst));  // open: en
  Register #(.width(32)) register_2 (.D(rs1), .Q(rs1_2), .clk(clk), .clr(rst));  // open: en
  Register #(.width(32)) register_3 (.D(rs2), .Q(rs2_2), .clk(clk), .clr(rst));  // open: en
  Register #(.width(32)) register_4 (.D(Immediate), .Q(Immediate_2), .clk(clk), .clr(rst));  // open: en
  Register #(.width(32)) register_5 (.D(Instruction), .Q(Instruction_2), .clk(clk), .clr(rst));  // open: en
  Register #(.width(5)) register_6 (.D(WriteDir), .Q(WriteDir_2), .clk(clk), .clr(rst));  // open: en
  Register #(.width(5)) register_7 (.D(ReadDir1), .Q(ReadDir1_2), .clk(clk), .clr(rst));  // open: en
  Register #(.width(5)) register_8 (.D(ReadDir2), .Q(ReadDir2_2), .clk(clk), .clr(rst));  // open: en
  Register #(.width(1)) register_9 (.D(RegWrite), .Q(RegWrite_2), .clk(clk), .clr(rst));  // open: en
  Register #(.width(1)) register_10 (.D(MemtoReg), .Q(MemtoReg_2), .clk(clk), .clr(rst));  // open: en
  Register #(.width(1)) register_11 (.D(Branch), .Q(Branch_2), .clk(clk), .clr(rst));  // open: en
  Register #(.width(1)) register_12 (.D(MemWrite), .Q(MemWrite_2), .clk(clk), .clr(rst));  // open: en
  Register #(.width(1)) register_13 (.D(MemRead), .Q(MemRead_2), .clk(clk), .clr(rst));  // open: en
  Register #(.width(1)) register_14 (.D(ALUSrc), .Q(ALUSrc_2), .clk(clk), .clr(rst));  // open: en
  Register #(.width(5)) register_15 (.D(ALUOp), .Q(ALUOp_2), .clk(clk), .clr(rst));  // open: en

  // Notes on the sheet:
  //   DATAPATH
  //   FORWARDING
  //   CONTROL
  //   WB
  //   MEM
  //   EX
endmodule

module EX_MEM (
  input  clk,
  input  rst,
  input  [31:0] PCBranch,
  input  RegWrite,
  input  MemtoReg,
  input  Zero,
  input  [31:0] ALUOutput,
  input  Branch,
  input  MemWrite,
  input  [31:0] rs2,
  input  MemRead,
  input  [4:0] WriteDir,
  output [31:0] PCBranch_2,
  output RegWrite_2,
  output MemtoReg_2,
  output Zero_2,
  output [31:0] ALUOutput_2,
  output Branch_2,
  output MemWrite_2,
  output [31:0] rs2_2,
  output MemRead_2,
  output [4:0] WriteDir_2
);

  Register #(.width(32)) register_1 (.D(PCBranch), .Q(PCBranch_2), .clk(clk), .clr(rst));  // open: en
  Register #(.width(1)) register_2 (.D(Zero), .Q(Zero_2), .clk(clk), .clr(rst));  // open: en
  Register #(.width(32)) register_3 (.D(ALUOutput), .Q(ALUOutput_2), .clk(clk), .clr(rst));  // open: en
  Register #(.width(32)) register_4 (.D(rs2), .Q(rs2_2), .clk(clk), .clr(rst));  // open: en
  Register #(.width(5)) register_5 (.D(WriteDir), .Q(WriteDir_2), .clk(clk), .clr(rst));  // open: en
  Register #(.width(1)) register_6 (.D(RegWrite), .Q(RegWrite_2), .clk(clk), .clr(rst));  // open: en
  Register #(.width(1)) register_7 (.D(MemtoReg), .Q(MemtoReg_2), .clk(clk), .clr(rst));  // open: en
  Register #(.width(1)) register_8 (.D(Branch), .Q(Branch_2), .clk(clk), .clr(rst));  // open: en
  Register #(.width(1)) register_9 (.D(MemWrite), .Q(MemWrite_2), .clk(clk), .clr(rst));  // open: en
  Register #(.width(1)) register_10 (.D(MemRead), .Q(MemRead_2), .clk(clk), .clr(rst));  // open: en

  // Notes on the sheet:
  //   DATAPATH
  //   CONTROL
  //   WB
  //   MEM
endmodule

module MEM_WB (
  input  clk,
  input  rst,
  input  [31:0] ALUOutput,
  input  RegWrite,
  input  MemtoReg,
  input  [31:0] DataOutput,
  input  [4:0] WriteDir,
  output [31:0] ALUOutput_2,
  output RegWrite_2,
  output MemtoReg_2,
  output [31:0] DataOutput_2,
  output [4:0] WriteDir_2
);

  Register #(.width(32)) register_1 (.D(ALUOutput), .Q(ALUOutput_2), .clk(clk), .clr(rst));  // open: en
  Register #(.width(32)) register_2 (.D(DataOutput), .Q(DataOutput_2), .clk(clk), .clr(rst));  // open: en
  Register #(.width(5)) register_3 (.D(WriteDir), .Q(WriteDir_2), .clk(clk), .clr(rst));  // open: en
  Register #(.width(1)) register_4 (.D(RegWrite), .Q(RegWrite_2), .clk(clk), .clr(rst));  // open: en
  Register #(.width(1)) register_5 (.D(MemtoReg), .Q(MemtoReg_2), .clk(clk), .clr(rst));  // open: en

  // Notes on the sheet:
  //   DATAPATH
  //   CONTROL
  //   WB
endmodule

module Forwarding (
  input  [4:0] ReadDir1,
  input  [4:0] ReadDir2,
  input  [31:0] EX_MEMrd,
  input  EX_MEMRegWrite,
  input  [31:0] MEM_WBrd,
  input  MEM_WBRegWrite,
  input  ALUsrc,
  output [1:0] ForwardA,
  output [1:0] ForwardB
);


  // Notes on the sheet:
  //   if (MEM/WB.RegWrite and (MEM/WB.RegisterRd ≠ 0) and not(EX/MEM.RegWrite and (EX/MEM.RegisterRd ≠ 0) and (EX/MEM.RegisterRd = ID/EX.RegisterRs1)) and (MEM/WB.RegisterRd = ID/EX.RegisterRs1)) ForwardA = 01
  //   if (MEM/WB.RegWrite and (MEM/WB.RegisterRd ≠ 0) and not(EX/MEM.RegWrite and (EX/MEM.RegisterRd ≠ 0) and (EX/MEM.RegisterRd = ID/EX.RegisterRs2)) and (MEM/WB.RegisterRd = ID/EX.RegisterRs2)) ForwardB = 01
endmodule

module Hazard_Detection (
  input  ID_EXMemRead,
  input  ID_EXWriteDir,
  input  [31:0] Instruction,
  output PCWrite,
  output IFWrite,
  output Stall,
  output Flush
);


  // Notes on the sheet:
  //   La idea es implementar la instrucción nop y en el caso de que se deba producir una bubble, detener la escritura ENABLE del PC y IFIDreg y sustituir la instrucción por un NOP
  //   Mala opción usar un nop como stall. Razón word bibliografía.
endmodule
